# Fritzing sketch CORE  PRACTICAL 11 FINAL (saved by Fritzing 0.9.3b)
circuit board: 8.46667cm x 5.64444cm
breadboards: 1

parts:
  C1 = Electrolytic Capacitor [capacitance=100µF package="100 mil [THT, electrolytic]"]
  R1 = Resistor [tolerance=±5% resistance=1M package=THT]
  D1 = Rectifier Diode [part_number=1N4001 package="300 mil [THT]"]
  Q1 = NPN-Transistor [package="TO92 [THT]"]
  R2 = Resistor [tolerance=±5% resistance=1k package=THT]
  R3 = Resistor [tolerance=±5% resistance=220 package=THT]
  Part1 = Arduino Uno (Rev3)

nets:
  N1: C1.-, D1.cathode, Q1.C, Part1.A1
  N2: C1.+, R1.Pin_0, Part1.A0, Part1.5V
  N3: R1.Pin_1, D1.anode
  N4: Q1.E, R3.Pin_0
  N5: Q1.B, R2.Pin_1
  N6: R2.Pin_0, Part1.D8
  N7: R3.Pin_1, Part1.GND

// code stored in the sketch: CORE PRACTICAL 11 FINAL.ino
#include <SoftwareSerial.h>

int charging = 8;       // the number of the charging transistor

int charge = true;    // charge to toggle
int analog_value = analogRead(A5);
int input_voltage = (analog_value * 5.0) / 1024.0;
int starttime = 0;
//int pointcount = 0;

long timer = 0;
int tcheck = false;

void setup()
{
  pinMode(charging, OUTPUT);
  pinMode(LED_BUILTIN, OUTPUT); //LED to check current status
  pinMode(A5, INPUT);

  Serial.begin(9600);
    while (!Serial) {
      ; // wait for serial port to connect. Needed for native USB port only
    }
}

void loop()
{
  int sensorValuen = analogRead(A0);
  float voltagen = sensorValuen * (5.0 / 1023.0);
  int sensorValuep = analogRead(A1);
  float voltagep = sensorValuep * (5.0 / 1023.0);
  float voltage = voltagep - voltagen;
  
      if (charge == true){ // toggles charging to have a high voltage (5V), activating the bridge on the transistor
        digitalWrite(charging, HIGH);
        digitalWrite(LED_BUILTIN, HIGH); //LED comes on to tell us it is charging
        if (voltage > 4.01) {
          charge = false;
          tcheck = true;
        }
      } else {  //toggles charging to have a low voltage (<1V), turning off the status LED as well.
        digitalWrite(charging, LOW);
        digitalWrite(LED_BUILTIN, LOW);
        //tcheck = true; 
      }
    
  if (charge == false) {
    if (voltage < 4.01 && voltage > 1.0) {
      if (tcheck == true) {
        starttime = millis();
        tcheck = false;
      }
      timer = millis() - starttime;
      Serial.print(timer);
      Serial.print(",");
      Serial.println(voltage);
      //pointcount += 1;
    }
    if (voltage < 1.0) {
      Serial.println(255);
      //Serial.println(pointcount);
      charge = true;
    }
  }
}
